// Logisim project assign1.circ as structural Verilog: 8 circuits, main circuit main
module main (
  input  [3:0] in_1
);

  wire A_output, B_output, C_output, D_output, E_output, F_output, G_output;

  BDriver B (
    .Input_2_0__I0(in_1[0]), .Input_2_1__I1(in_1[1]), .Input_2_2__I2(in_1[2]), .Input_2_3__I3(in_1[3]),
    .Output(B_output));
  ADriver A (
    .Input_2_0__I0(in_1[0]), .Input_2_1__I1(in_1[1]), .Input_2_2__I2(in_1[2]), .Input_2_3__I3(in_1[3]),
    .Output(A_output));
  FDriver F (
    .Input_2_0__I0(in_1[0]), .Input_2_1__I1(in_1[1]), .Input_2_2__I2(in_1[2]), .Input_2_3__I3(in_1[3]),
    .Output(F_output));
  GDriver G (
    .Input_2_0__I0(in_1[0]), .Input_2_1__I1(in_1[1]), .Input_2_2__I2(in_1[2]), .Input_2_3__I3(in_1[3]),
    .Output(G_output));
  EDriver E (
    .Input_2_0__I0(in_1[0]), .Input_2_1__I1(in_1[1]), .Input_2_2__I2(in_1[2]), .Input_2_3__I3(in_1[3]),
    .Output(E_output));
  DDriver D (
    .Input_2_0__I0(in_1[0]), .Input_2_1__I1(in_1[1]), .Input_2_2__I2(in_1[2]), .Input_2_3__I3(in_1[3]),
    .Output(D_output));
  CDriver C (
    .Input_2_0__I0(in_1[0]), .Input_2_1__I1(in_1[1]), .Input_2_2__I2(in_1[2]), .Input_2_3__I3(in_1[3]),
    .Output(C_output));
  _7_Segment_Display u_7_segment_display_1 (
    .g(G_output), .f(F_output), .a(A_output), .b(B_output), .e(E_output), .d(D_output), .c(C_output));  // open: dp
endmodule

module ADriver (
  input  Input_2_0__I0,
  input  Input_2_1__I1,
  input  Input_2_2__I2,
  input  Input_2_3__I3,
  output Output
);

  wire and_1_out, and_2_out, and_3_out, and_4_out, not_1_out, not_2_out, not_3_out, not_4_out, not_5_out,
       not_6_out, or_1_out, or_2_out;

  not not_1 (not_1_out, Input_2_0__I0);
  not not_2 (not_2_out, Input_2_2__I2);
  not not_3 (not_3_out, Input_2_3__I3);
  not not_4 (not_4_out, Input_2_3__I3);
  not not_5 (not_5_out, Input_2_1__I1);
  not not_6 (not_6_out, Input_2_2__I2);
  or or_1 (or_1_out, not_2_out, Input_2_3__I3);
  or or_2 (or_2_out, Input_2_2__I2, not_3_out);
  and and_1 (and_1_out, Input_2_0__I0, Input_2_2__I2, not_4_out);
  and and_2 (and_2_out, not_5_out, not_6_out, Input_2_3__I3);
  and and_3 (and_3_out, not_1_out, or_1_out);
  and and_4 (and_4_out, Input_2_1__I1, or_2_out);
  or or_3 (Output, and_2_out, and_1_out, and_4_out, and_3_out);
endmodule

module BDriver (
  input  Input_2_0__I0,
  input  Input_2_1__I1,
  input  Input_2_2__I2,
  input  Input_2_3__I3,
  output Output
);

  wire and_1_out, and_2_out, and_3_out, not_1_out, not_2_out, not_3_out, not_4_out, not_5_out, not_6_out,
       or_1_out, xor_1_out;

  not not_1 (not_1_out, Input_2_0__I0);
  or or_1 (or_1_out, not_1_out, not_2_out);
  not not_2 (not_2_out, Input_2_3__I3);
  xor xor_1 (xor_1_out, Input_2_1__I1, Input_2_3__I3);
  not not_3 (not_3_out, Input_2_0__I0);
  not not_4 (not_4_out, Input_2_1__I1);
  not not_5 (not_5_out, Input_2_3__I3);
  not not_6 (not_6_out, Input_2_2__I2);
  and and_1 (and_1_out, Input_2_0__I0, xor_1_out);
  and and_2 (and_2_out, not_3_out, not_4_out, not_5_out);
  and and_3 (and_3_out, not_6_out, or_1_out);
  or or_2 (Output, and_2_out, and_1_out, and_3_out);
endmodule

module CDriver (
  input  Input_2_0__I0,
  input  Input_2_1__I1,
  input  Input_2_2__I2,
  input  Input_2_3__I3,
  output Output
);

  wire and_1_out, and_2_out, not_1_out, not_2_out, or_1_out, xor_1_out;

  not not_1 (not_1_out, Input_2_1__I1);
  or or_1 (or_1_out, Input_2_0__I0, not_1_out);
  not not_2 (not_2_out, Input_2_3__I3);
  or or_2 (Output, xor_1_out, and_1_out, and_2_out);
  and and_1 (and_1_out, or_1_out, not_2_out);
  xor xor_1 (xor_1_out, Input_2_2__I2, Input_2_3__I3);
  and and_2 (and_2_out, Input_2_0__I0, not_1_out);
endmodule

module DDriver (
  input  Input_2_0__I0,
  input  Input_2_1__I1,
  input  Input_2_2__I2,
  input  Input_2_3__I3,
  output Output
);

  wire and_1_out, and_2_out, and_3_out, and_4_out, and_5_out, not_1_out, not_2_out, not_3_out, not_4_out,
       or_1_out, xor_1_out;

  not not_1 (not_1_out, Input_2_2__I2);
  not not_2 (not_2_out, Input_2_3__I3);
  xor xor_1 (xor_1_out, Input_2_1__I1, Input_2_2__I2);
  and and_1 (and_1_out, not_1_out, not_2_out);
  and and_2 (and_2_out, Input_2_1__I1, Input_2_2__I2);
  not not_3 (not_3_out, Input_2_1__I1);
  and and_3 (and_3_out, Input_2_0__I0, xor_1_out);
  not not_4 (not_4_out, Input_2_0__I0);
  or or_1 (or_1_out, and_1_out, and_2_out);
  and and_4 (and_4_out, not_3_out, Input_2_3__I3);
  and and_5 (and_5_out, not_4_out, or_1_out);
  or or_2 (Output, and_4_out, and_5_out, and_3_out);
endmodule

module EDriver (
  input  Input_2_0__I0,
  input  Input_2_1__I1,
  input  Input_2_2__I2,
  input  Input_2_3__I3,
  output Output
);

  wire and_1_out, and_2_out, not_1_out, not_2_out, or_1_out, or_2_out;

  not not_1 (not_1_out, Input_2_2__I2);
  not not_2 (not_2_out, Input_2_0__I0);
  or or_1 (or_1_out, Input_2_1__I1, not_1_out);
  or or_2 (or_2_out, Input_2_1__I1, Input_2_2__I2);
  and and_1 (and_1_out, not_2_out, or_1_out);
  and and_2 (and_2_out, or_2_out, Input_2_3__I3);
  or or_3 (Output, and_2_out, and_1_out);
endmodule

module FDriver (
  input  Input_2_0__I0,
  input  Input_2_1__I1,
  input  Input_2_2__I2,
  input  Input_2_3__I3,
  output Output
);

  wire and_1_out, and_2_out, and_3_out, and_4_out, not_1_out, not_2_out, not_3_out, not_4_out, not_5_out,
       or_1_out, or_2_out;

  not not_1 (not_1_out, Input_2_1__I1);
  and and_1 (and_1_out, Input_2_1__I1, Input_2_2__I2);
  not not_2 (not_2_out, Input_2_2__I2);
  not not_3 (not_3_out, Input_2_1__I1);
  not not_4 (not_4_out, Input_2_3__I3);
  not not_5 (not_5_out, Input_2_0__I0);
  or or_1 (or_1_out, not_1_out, and_1_out);
  or or_2 (or_2_out, Input_2_1__I1, not_2_out);
  and and_2 (and_2_out, not_3_out, Input_2_2__I2, not_4_out);
  and and_3 (and_3_out, not_5_out, or_1_out);
  and and_4 (and_4_out, Input_2_3__I3, or_2_out);
  or or_3 (Output, and_2_out, and_4_out, and_3_out);
endmodule

module GDriver (
  input  Input_2_0__I0,
  input  Input_2_1__I1,
  input  Input_2_2__I2,
  input  Input_2_3__I3,
  output Output
);

  wire and_1_out, and_2_out, and_3_out, and_4_out, and_5_out, not_1_out, not_2_out, not_3_out, not_4_out,
       not_5_out, or_1_out;

  not not_1 (not_1_out, Input_2_2__I2);
  not not_2 (not_2_out, Input_2_0__I0);
  not not_3 (not_3_out, Input_2_2__I2);
  not not_4 (not_4_out, Input_2_1__I1);
  not not_5 (not_5_out, Input_2_3__I3);
  and and_1 (and_1_out, Input_2_1__I1, not_1_out);
  and and_2 (and_2_out, not_2_out, Input_2_1__I1);
  and and_3 (and_3_out, not_3_out, Input_2_3__I3);
  and and_4 (and_4_out, not_4_out, Input_2_2__I2, not_5_out);
  or or_1 (or_1_out, Input_2_3__I3, and_1_out);
  and and_5 (and_5_out, Input_2_0__I0, or_1_out);
  or or_2 (Output, and_4_out, and_3_out, and_2_out, and_5_out);
endmodule
