// Logisim project assign1bonus.circ as structural Verilog: 11 circuits, main circuit main
module main (
);

  wire A_output, B_output, button_1_out, button_2_out, C_output, D_output, E_output, F_output, G_output,
       or_1_out;
  wire [3:0] multiplexer_1_out, n1bitmem_1_output, n4bitadder_1_output;

  Button button_1 (.out(button_1_out));
  Button button_2 (.out(button_2_out));
  _4bitAdder u_4bitadder_1 (.Input(n1bitmem_1_output), .Button(button_1_out), .Output(n4bitadder_1_output));
  Multiplexer #(.width(4)) multiplexer_1 (
    .in0(n4bitadder_1_output), .in1(4'b0000), .out(multiplexer_1_out), .sel(button_2_out));  // open: en
  or or_1 (or_1_out, button_1_out, button_2_out);
  _1BitMem u_1bitmem_1 (.CLK(or_1_out), .Data(multiplexer_1_out[0]), .Output(n1bitmem_1_output[0]));
  _1BitMem u_1bitmem_2 (.CLK(or_1_out), .Data(multiplexer_1_out[1]), .Output(n1bitmem_1_output[1]));
  _1BitMem u_1bitmem_3 (.CLK(or_1_out), .Data(multiplexer_1_out[2]), .Output(n1bitmem_1_output[2]));
  _1BitMem u_1bitmem_4 (.CLK(or_1_out), .Data(multiplexer_1_out[3]), .Output(n1bitmem_1_output[3]));
  BDriver B (
    .Input_2_0__I0(n1bitmem_1_output[0]), .Input_2_1__I1(n1bitmem_1_output[1]),
    .Input_2_2__I2(n1bitmem_1_output[2]), .Input_2_3__I3(n1bitmem_1_output[3]), .Output(B_output));
  ADriver A (
    .Input_2_0__I0(n1bitmem_1_output[0]), .Input_2_1__I1(n1bitmem_1_output[1]),
    .Input_2_2__I2(n1bitmem_1_output[2]), .Input_2_3__I3(n1bitmem_1_output[3]), .Output(A_output));
  FDriver F (
    .Input_2_0__I0(n1bitmem_1_output[0]), .Input_2_1__I1(n1bitmem_1_output[1]),
    .Input_2_2__I2(n1bitmem_1_output[2]), .Input_2_3__I3(n1bitmem_1_output[3]), .Output(F_output));
  GDriver G (
    .Input_2_0__I0(n1bitmem_1_output[0]), .Input_2_1__I1(n1bitmem_1_output[1]),
    .Input_2_2__I2(n1bitmem_1_output[2]), .Input_2_3__I3(n1bitmem_1_output[3]), .Output(G_output));
  EDriver E (
    .Input_2_0__I0(n1bitmem_1_output[0]), .Input_2_1__I1(n1bitmem_1_output[1]),
    .Input_2_2__I2(n1bitmem_1_output[2]), .Input_2_3__I3(n1bitmem_1_output[3]), .Output(E_output));
  DDriver D (
    .Input_2_0__I0(n1bitmem_1_output[0]), .Input_2_1__I1(n1bitmem_1_output[1]),
    .Input_2_2__I2(n1bitmem_1_output[2]), .Input_2_3__I3(n1bitmem_1_output[3]), .Output(D_output));
  CDriver C (
    .Input_2_0__I0(n1bitmem_1_output[0]), .Input_2_1__I1(n1bitmem_1_output[1]),
    .Input_2_2__I2(n1bitmem_1_output[2]), .Input_2_3__I3(n1bitmem_1_output[3]), .Output(C_output));
  _7_Segment_Display u_7_segment_display_1 (
    .g(G_output), .f(F_output), .a(A_output), .b(B_output), .e(E_output), .d(D_output), .c(C_output));  // open: dp

  // Notes on the sheet:
  //   Increment
  //   Reset Memory
  //   Adder
  //   Note: Please press this button at beginning of program to set memory to 0
  //   Memory Unit
  //   7-Segment Decoders
endmodule

module ADriver (
  input  Input_2_0__I0,
  input  Input_2_1__I1,
  input  Input_2_2__I2,
  input  Input_2_3__I3,
  output Output
);

  wire and_1_out, and_2_out, and_3_out, and_4_out, not_1_out, not_2_out, not_3_out, not_4_out, not_5_out,
       not_6_out, or_1_out, or_2_out;

  not not_1 (not_1_out, Input_2_0__I0);
  not not_2 (not_2_out, Input_2_2__I2);
  not not_3 (not_3_out, Input_2_3__I3);
  not not_4 (not_4_out, Input_2_3__I3);
  not not_5 (not_5_out, Input_2_1__I1);
  not not_6 (not_6_out, Input_2_2__I2);
  or or_1 (or_1_out, not_2_out, Input_2_3__I3);
  or or_2 (or_2_out, Input_2_2__I2, not_3_out);
  and and_1 (and_1_out, Input_2_0__I0, Input_2_2__I2, not_4_out);
  and and_2 (and_2_out, not_5_out, not_6_out, Input_2_3__I3);
  and and_3 (and_3_out, not_1_out, or_1_out);
  and and_4 (and_4_out, Input_2_1__I1, or_2_out);
  or or_3 (Output, and_2_out, and_1_out, and_4_out, and_3_out);
endmodule

module BDriver (
  input  Input_2_0__I0,
  input  Input_2_1__I1,
  input  Input_2_2__I2,
  input  Input_2_3__I3,
  output Output
);

  wire and_1_out, and_2_out, and_3_out, not_1_out, not_2_out, not_3_out, not_4_out, not_5_out, not_6_out,
       or_1_out, xor_1_out;

  not not_1 (not_1_out, Input_2_0__I0);
  or or_1 (or_1_out, not_1_out, not_2_out);
  not not_2 (not_2_out, Input_2_3__I3);
  xor xor_1 (xor_1_out, Input_2_1__I1, Input_2_3__I3);
  not not_3 (not_3_out, Input_2_0__I0);
  not not_4 (not_4_out, Input_2_1__I1);
  not not_5 (not_5_out, Input_2_3__I3);
  not not_6 (not_6_out, Input_2_2__I2);
  and and_1 (and_1_out, Input_2_0__I0, xor_1_out);
  and and_2 (and_2_out, not_3_out, not_4_out, not_5_out);
  and and_3 (and_3_out, not_6_out, or_1_out);
  or or_2 (Output, and_2_out, and_1_out, and_3_out);
endmodule

module CDriver (
  input  Input_2_0__I0,
  input  Input_2_1__I1,
  input  Input_2_2__I2,
  input  Input_2_3__I3,
  output Output
);

  wire and_1_out, and_2_out, not_1_out, not_2_out, or_1_out, xor_1_out;

  not not_1 (not_1_out, Input_2_1__I1);
  or or_1 (or_1_out, Input_2_0__I0, not_1_out);
  not not_2 (not_2_out, Input_2_3__I3);
  or or_2 (Output, xor_1_out, and_1_out, and_2_out);
  and and_1 (and_1_out, or_1_out, not_2_out);
  xor xor_1 (xor_1_out, Input_2_2__I2, Input_2_3__I3);
  and and_2 (and_2_out, Input_2_0__I0, not_1_out);
endmodule

module DDriver (
  input  Input_2_0__I0,
  input  Input_2_1__I1,
  input  Input_2_2__I2,
  input  Input_2_3__I3,
  output Output
);

  wire and_1_out, and_2_out, and_3_out, and_4_out, and_5_out, not_1_out, not_2_out, not_3_out, not_4_out,
       or_1_out, xor_1_out;

  not not_1 (not_1_out, Input_2_2__I2);
  not not_2 (not_2_out, Input_2_3__I3);
  xor xor_1 (xor_1_out, Input_2_1__I1, Input_2_2__I2);
  and and_1 (and_1_out, not_1_out, not_2_out);
  and and_2 (and_2_out, Input_2_1__I1, Input_2_2__I2);
  not not_3 (not_3_out, Input_2_1__I1);
  and and_3 (and_3_out, Input_2_0__I0, xor_1_out);
  not not_4 (not_4_out, Input_2_0__I0);
  or or_1 (or_1_out, and_1_out, and_2_out);
  and and_4 (and_4_out, not_3_out, Input_2_3__I3);
  and and_5 (and_5_out, not_4_out, or_1_out);
  or or_2 (Output, and_4_out, and_5_out, and_3_out);
endmodule

module EDriver (
  input  Input_2_0__I0,
  input  Input_2_1__I1,
  input  Input_2_2__I2,
  input  Input_2_3__I3,
  output Output
);

  wire and_1_out, and_2_out, not_1_out, not_2_out, or_1_out, or_2_out;

  not not_1 (not_1_out, Input_2_2__I2);
  not not_2 (not_2_out, Input_2_0__I0);
  or or_1 (or_1_out, Input_2_1__I1, not_1_out);
  or or_2 (or_2_out, Input_2_1__I1, Input_2_2__I2);
  and and_1 (and_1_out, not_2_out, or_1_out);
  and and_2 (and_2_out, or_2_out, Input_2_3__I3);
  or or_3 (Output, and_2_out, and_1_out);
endmodule

module FDriver (
  input  Input_2_0__I0,
  input  Input_2_1__I1,
  input  Input_2_2__I2,
  input  Input_2_3__I3,
  output Output
);

  wire and_1_out, and_2_out, and_3_out, and_4_out, not_1_out, not_2_out, not_3_out, not_4_out, not_5_out,
       or_1_out, or_2_out;

  not not_1 (not_1_out, Input_2_1__I1);
  and and_1 (and_1_out, Input_2_1__I1, Input_2_2__I2);
  not not_2 (not_2_out, Input_2_2__I2);
  not not_3 (not_3_out, Input_2_1__I1);
  not not_4 (not_4_out, Input_2_3__I3);
  not not_5 (not_5_out, Input_2_0__I0);
  or or_1 (or_1_out, not_1_out, and_1_out);
  or or_2 (or_2_out, Input_2_1__I1, not_2_out);
  and and_2 (and_2_out, not_3_out, Input_2_2__I2, not_4_out);
  and and_3 (and_3_out, not_5_out, or_1_out);
  and and_4 (and_4_out, Input_2_3__I3, or_2_out);
  or or_3 (Output, and_2_out, and_4_out, and_3_out);
endmodule

module GDriver (
  input  Input_2_0__I0,
  input  Input_2_1__I1,
  input  Input_2_2__I2,
  input  Input_2_3__I3,
  output Output
);

  wire and_1_out, and_2_out, and_3_out, and_4_out, and_5_out, not_1_out, not_2_out, not_3_out, not_4_out,
       not_5_out, or_1_out;

  not not_1 (not_1_out, Input_2_2__I2);
  not not_2 (not_2_out, Input_2_0__I0);
  not not_3 (not_3_out, Input_2_2__I2);
  not not_4 (not_4_out, Input_2_1__I1);
  not not_5 (not_5_out, Input_2_3__I3);
  and and_1 (and_1_out, Input_2_1__I1, not_1_out);
  and and_2 (and_2_out, not_2_out, Input_2_1__I1);
  and and_3 (and_3_out, not_3_out, Input_2_3__I3);
  and and_4 (and_4_out, not_4_out, Input_2_2__I2, not_5_out);
  or or_1 (or_1_out, Input_2_3__I3, and_1_out);
  and and_5 (and_5_out, Input_2_0__I0, or_1_out);
  or or_2 (Output, and_4_out, and_3_out, and_2_out, and_5_out);
endmodule

module _1BitMem (
  input  CLK,
  input  Data,
  output Output
);

  wire nand_1_out, nand_2_out, nand_3_out, nand_4_out, nand_6_out, not_1_out;

  not not_1 (not_1_out, CLK);
  nand nand_1 (nand_1_out, nand_4_out, nand_2_out);
  nand nand_2 (nand_2_out, nand_1_out, not_1_out);
  nand nand_3 (nand_3_out, nand_2_out, not_1_out, nand_4_out);
  nand nand_4 (nand_4_out, nand_3_out, Data);
  nand nand_5 (Output, nand_2_out, nand_6_out);
  nand nand_6 (nand_6_out, Output, nand_3_out);
endmodule

module Adder (
  input  A,
  input  B,
  input  Carry_in,
  output Output,
  output Carry_out
);

  wire and_1_out, and_2_out, xor_1_out;

  xor xor_1 (xor_1_out, A, B);
  xor xor_2 (Output, xor_1_out, Carry_in);
  and and_1 (and_1_out, xor_1_out, Carry_in);
  and and_2 (and_2_out, A, B);
  or or_1 (Carry_out, and_1_out, and_2_out);
endmodule

module _4bitAdder (
  input  [3:0] Input,
  input  Button,
  output [3:0] Output
);

  wire adder_1_carry_out, adder_2_carry_out, adder_3_carry_out;

  Adder adder_1 (.A(Button), .B(Input[0]), .Carry_in(1'b0), .Output(Output[0]), .Carry_out(adder_1_carry_out));
  Adder adder_2 (
    .A(1'b0), .B(Input[1]), .Carry_in(adder_1_carry_out), .Output(Output[1]), .Carry_out(adder_2_carry_out));
  Adder adder_3 (
    .A(1'b0), .B(Input[2]), .Carry_in(adder_2_carry_out), .Output(Output[2]), .Carry_out(adder_3_carry_out));
  Adder adder_4 (.A(1'b0), .B(Input[3]), .Carry_in(adder_3_carry_out), .Output(Output[3]));  // open: Carry_out
endmodule
