// Logisim project assign2.circ as structural Verilog: 5 circuits, main circuit main
module main (
  input  Direction,
  input  Enable
);

  wire bintogray_1_g1, bintogray_1_g2, bintogray_1_g3, CLK_out;
  wire [2:0] memory_a_1_output_q;

  Clock CLK (.out(CLK_out));
  Memory_A memory_a_1 (
    .A(memory_a_1_output_q[0]), .B(memory_a_1_output_q[1]), .C(memory_a_1_output_q[2]), .D(Direction),
    .E(Enable), .CLK(CLK_out), .Output_Q(memory_a_1_output_q[0]));
  Memory_B memory_b_1 (
    .A(memory_a_1_output_q[0]), .B(memory_a_1_output_q[1]), .C(memory_a_1_output_q[2]), .D(Direction),
    .E(Enable), .CLK(CLK_out), .Output_Q(memory_a_1_output_q[1]));
  Memory_C memory_c_1 (
    .A(memory_a_1_output_q[0]), .B(memory_a_1_output_q[1]), .C(memory_a_1_output_q[2]), .D(Direction),
    .E(Enable), .CLK(CLK_out), .Output_Q(memory_a_1_output_q[2]));
  LED led_1 (.in(bintogray_1_g1));
  BinToGray bintogray_1 (
    .A(memory_a_1_output_q[0]), .B(memory_a_1_output_q[1]), .C(memory_a_1_output_q[2]), .G1(bintogray_1_g1),
    .G2(bintogray_1_g2), .G3(bintogray_1_g3));
  LED led_2 (.in(bintogray_1_g2));
  LED led_3 (.in(bintogray_1_g3));

  // Notes on the sheet:
  //   Gray Code
endmodule

module BinToGray (
  input  A,
  input  B,
  input  C,
  output G1,
  output G2,
  output G3
);

  xor xor_1 (G2, A, B);
  xor xor_2 (G3, B, C);

  assign G1 = A;
endmodule

module Memory_A (
  input  CLK,
  input  A,
  input  B,
  input  C,
  input  D,
  input  E,
  output Output_Q
);

  wire and_1_out, and_2_out, and_3_out, not_1_out, not_2_out, not_3_out, or_1_out;

  not not_1 (not_1_out, D);
  not not_2 (not_2_out, B);
  not not_3 (not_3_out, C);
  and and_1 (and_1_out, B, C, not_1_out);
  and and_2 (and_2_out, not_2_out, not_3_out, D);
  or or_1 (or_1_out, and_1_out, and_2_out);
  and and_3 (and_3_out, or_1_out, E);
  J_K_Flip_Flop j_k_ff_1 (.J(and_3_out), .clk(CLK), .K(and_3_out), .Q(Output_Q));  // open: Qn, preset, en, reset
endmodule

module Memory_B (
  input  CLK,
  input  A,
  input  B,
  input  C,
  input  D,
  input  E,
  output Output_Q
);

  wire and_1_out, xor_1_out;

  xor xor_1 (xor_1_out, C, D);
  and and_1 (and_1_out, xor_1_out, E);
  J_K_Flip_Flop j_k_ff_1 (.J(and_1_out), .clk(CLK), .K(and_1_out), .Q(Output_Q));  // open: Qn, preset, en, reset
endmodule

module Memory_C (
  input  CLK,
  input  A,
  input  B,
  input  C,
  input  D,
  input  E,
  output Output_Q
);

  J_K_Flip_Flop j_k_ff_1 (.J(E), .clk(CLK), .K(E), .Q(Output_Q));  // open: Qn, preset, en, reset
endmodule
