// Logisim project T03_3BitAdderSubtractor.circ as structural Verilog: 1 circuit, main circuit main
module main (
  input  x,
  input  y,
  input  z
);

  wire and_1_out, and_2_out, and_3_out, and_4_out, and_5_out, and_6_out, and_7_out, not_1_out, not_2_out,
       not_3_out, or_1_out, or_2_out, or_3_out;

  and and_1 (and_1_out, x, y);
  and and_2 (and_2_out, y, z);
  not not_1 (not_1_out, x);
  not not_2 (not_2_out, y);
  not not_3 (not_3_out, z);
  or or_1 (or_1_out, and_1_out, and_2_out);
  and and_3 (and_3_out, not_3_out, not_1_out);
  and and_4 (and_4_out, x, z);
  and and_5 (and_5_out, x, not_2_out);
  and and_6 (and_6_out, not_2_out, z);
  and and_7 (and_7_out, not_1_out, y, not_3_out);
  or or_2 (or_2_out, and_5_out, and_5_out, and_6_out, and_7_out, and_7_out);
  or or_3 (or_3_out, and_3_out, and_3_out, and_3_out, and_4_out);
  LED led_1 (.in(or_1_out));
  LED led_2 (.in(or_2_out));
  LED led_3 (.in(or_3_out));

  // Notes on the sheet:
  //   This circuit adds 1 to the input if the input is less than 4, then outputs it. Otherwise, it subtracts the input by 2 then outputs it.
endmodule
