// Logisim project T04_grayCode_to_Binary.circ as structural Verilog: 1 circuit, main circuit main
module main (
  input  x,
  input  y,
  input  z
);

  wire xor_1_out, xor_2_out;

  xor xor_1 (xor_1_out, x, y);
  xor xor_2 (xor_2_out, y, z);
  LED a (.in(x));
  LED b (.in(xor_1_out));
  LED c (.in(xor_2_out));
endmodule
