// Logisim project T05&06LatchesandFlipFlips.circ as structural Verilog
module D_latch (
  input  CLK,
  input  D,
  output Q,
  output Q_prime
);

  wire and_1_out, and_2_out, not_1_out;

  not not_1 (not_1_out, D);
  and and_1 (and_1_out, not_1_out, CLK);
  and and_2 (and_2_out, CLK, D);
  nor nor_1 (Q, and_1_out, Q_prime);
  nor nor_2 (Q_prime, Q, and_2_out);
endmodule

module D_Flip_flop (
  input  CLK,
  input  Data,
  output Q,
  output Q_prime
);

  wire nand_1_out, nand_2_out, nand_3_out, nand_4_out;

  nand nand_1 (nand_1_out, nand_4_out, nand_2_out);
  nand nand_2 (nand_2_out, nand_1_out, CLK);
  nand nand_3 (nand_3_out, nand_2_out, CLK, nand_4_out);
  nand nand_4 (nand_4_out, nand_3_out, Data);
  nand nand_5 (Q, nand_2_out, Q_prime);
  nand nand_6 (Q_prime, Q, nand_3_out);
endmodule

module Shortened_D_flip_flop (
  input  Data,
  output Q,
  output Q_prime
);

  wire and_1_out, clock_1_out, s_r_latch_1_out_3, s_r_latch_1_out_4, s_r_latch_2_out_4;

  Clock clock_1 (.out(clock_1_out));
  S_R__Latch s_r_latch_1 (.in_1(and_1_out), .in_2(Data), .out_3(s_r_latch_1_out_3), .out_4(s_r_latch_1_out_4));
  and and_1 (and_1_out, s_r_latch_2_out_4, clock_1_out);
  S_R__Latch s_r_latch_2 (.in_1(s_r_latch_1_out_4), .in_2(clock_1_out), .out_4(s_r_latch_2_out_4));  // open: out_3
  S_R__Latch s_r_latch_3 (.in_1(s_r_latch_2_out_4), .in_2(s_r_latch_1_out_3), .out_3(Q), .out_4(Q_prime));
endmodule

module S_R__Latch (
  input  in_1,
  input  in_2,
  output out_3,
  output out_4
);

  nand nand_1 (out_3, in_1, out_4);
  nand nand_2 (out_4, out_3, in_2);
endmodule
