// Logisim project T08TFlipFlops.circ as structural Verilog: 4 circuits, main circuit main
module main (
  output y
);

  wire a_1_output, b_1_output, c_1_output, clock_1_out, not_1_out, t_ff_1_q, t_ff_2_q, t_ff_3_q, x_out;

  Button x (.out(x_out));
  A a_1 (.A(t_ff_1_q), .B(t_ff_2_q), .C(t_ff_3_q), .x(x_out), .Output(a_1_output));
  B b_1 (.A(t_ff_1_q), .B(t_ff_2_q), .C(t_ff_3_q), .x(x_out), .Output(b_1_output));
  C c_1 (.A(t_ff_1_q), .B(t_ff_2_q), .C(t_ff_3_q), .x(x_out), .Output(c_1_output));
  Clock clock_1 (.out(clock_1_out));
  T_Flip_Flop t_ff_1 (.clk(clock_1_out), .T(a_1_output), .Q(t_ff_1_q));  // open: Qn, preset, reset, en
  T_Flip_Flop t_ff_2 (.clk(clock_1_out), .T(b_1_output), .Q(t_ff_2_q));  // open: Qn, preset, reset, en
  T_Flip_Flop t_ff_3 (.clk(clock_1_out), .T(c_1_output), .Q(t_ff_3_q));  // open: Qn, preset, reset, en
  not not_1 (not_1_out, t_ff_1_q);
  and and_1 (y, not_1_out, x_out);

  // Notes on the sheet:
  //   Prety sure this works, not thorougly tested though...
endmodule

module A (
  input  A,
  input  B,
  input  C,
  input  x,
  output Output
);

  wire and_1_out, not_1_out;

  not not_1 (not_1_out, B);
  and and_1 (and_1_out, not_1_out, x);
  or or_1 (Output, A, and_1_out);
endmodule

module B (
  input  A,
  input  B,
  input  C,
  input  x,
  output Output
);

  wire and_1_out, and_2_out, not_1_out, not_2_out, not_3_out, xor_1_out;

  xor xor_1 (xor_1_out, C, x);
  and and_1 (and_1_out, B, xor_1_out);
  not not_1 (not_1_out, B);
  not not_2 (not_2_out, C);
  not not_3 (not_3_out, x);
  and and_2 (and_2_out, not_1_out, not_2_out, not_3_out);
  or or_1 (Output, A, and_1_out, and_2_out);
endmodule

module C (
  input  A,
  input  B,
  input  C,
  input  x,
  output Output
);

  wire and_1_out, and_2_out, not_1_out, not_2_out, not_3_out, not_4_out, or_1_out;

  not not_1 (not_1_out, A);
  not not_2 (not_2_out, B);
  not not_3 (not_3_out, C);
  not not_4 (not_4_out, x);
  or or_1 (or_1_out, C, A);
  and and_1 (and_1_out, not_1_out, not_2_out, not_3_out, not_4_out);
  and and_2 (and_2_out, x, or_1_out);
  or or_2 (Output, and_1_out, and_2_out);
endmodule
